# Fritzing sketch Breakoutboard (saved by Fritzing 0.9.2b)
circuit board: 8.46667cm x 5.64444cm
breadboards: 1

parts:
  JP3 = Header 5x2 [package=2x5-shrouded_smd]
  JP1 = Header 4 [package=molex-1x4_lock]
  JP4 = Header 4 [package=molex-1x4_lock]
  JP5 = Header 4 [package=molex-1x4_lock]
  JP6 = Header 4 [package=molex-1x4_lock]
  JP7 = Header 4 [package=molex-1x4_lock]
  JP8 = Header 4 [package=molex-1x4_lock]
  JP9 = Header 4 [package=molex-1x4_lock]
  JP10 = Header 4 [package=molex-1x4_lock]
  JP11 = Header 2 [package=molex-1x2_lock]
  JP12 = Header 4 [package=molex-1x4_lock]
  JP13 = Header 4 [package=molex-1x4_lock]
  JP16 = Header 2 [package=molex-1x2_lock]
  JP17 = Header 2 [package=molex-1x2_lock]
  JP18 = Header 2 [package=molex-1x2_lock]
  JP23 = Header 4 [package=molex-1x4_lock]
  JP24 = Header 4 [package=molex-1x4_lock]
  JP25 = Header 2 [package=molex-1x2_lock]

nets:
  N1: JP3.1, JP23.1
  N2: JP3.2, JP24.1
  N3: JP3.3, JP23.2
  N4: JP3.4, JP24.2
  N5: JP3.5, JP23.3
  N6: JP3.6, JP24.3
  N7: JP3.7, JP23.4
  N8: JP3.8, JP24.4
  N9: JP3.9, JP25.1
  N10: JP3.10, JP25.2
  N11: JP1.1, JP4.1
  N12: JP1.2, JP4.2
  N13: JP1.3, JP4.3
  N14: JP1.4, JP4.4
  N15: JP5.1, JP6.1
  N16: JP5.2, JP6.2
  N17: JP5.3, JP6.3
  N18: JP5.4, JP6.4
  N19: JP7.1, JP8.1
  N20: JP7.2, JP8.2
  N21: JP7.3, JP8.3
  N22: JP7.4, JP8.4
  N23: JP9.1, JP10.1
  N24: JP9.2, JP10.2
  N25: JP9.3, JP10.3
  N26: JP9.4, JP10.4
  N27: JP11.1, JP12.1
  N28: JP11.2, JP12.2
  N29: JP12.3, JP16.1
  N30: JP12.4, JP16.2
  N31: JP13.1, JP17.1
  N32: JP13.2, JP17.2
  N33: JP13.3, JP18.1
  N34: JP13.4, JP18.2
