# Fritzing sketch Breakoutboard (saved by Fritzing 0.9.2b)
circuit board: 4.47743cm x 4.5151cm
breadboards: 1

parts:
  M0_IN = Header 4 [package=molex-1x4_lock]
  M0_OUT = Header 4 [package=molex-1x4_lock]
  H0 = Header 2 [package=molex-1x2_lock]
  H01 = Header 4 [package=molex-1x4_lock]
  H1 = Header 2 [package=molex-1x2_lock]
  T01 = Header 4 [package=molex-1x4_lock]
  T23 = Header 4 [package=molex-1x4_lock]
  ES2 = Header 2 [package=molex-1x2_lock]
  ES1 = Header 2 [package=molex-1x2_lock]
  ES0 = Header 2 [package=molex-1x2_lock]
  M1_OUT = Header 4 [package=molex-1x4_lock]
  M1_IN = Header 4 [package=molex-1x4_lock]
  M2_OUT = Header 4 [package=molex-1x4_lock]
  M3_OUT = Header 4 [package=molex-1x4_lock]
  M2_IN = Header 4 [package=molex-1x4_lock]
  M3_IN = Header 4 [package=molex-1x4_lock]
  H23 = Header 4 [package=molex-1x4_lock]
  H3 = Header 2 [package=molex-1x2_lock]
  H2 = Header 2 [package=molex-1x2_lock]
  ESZ = Header 4 [package=molex-1x4_lock]
  TE = Header 5x2 [package=avr_icsp]

nets:
  N1: M0_IN.1, M0_OUT.1
  N2: M0_IN.2, M0_OUT.2
  N3: M0_IN.3, M0_OUT.3
  N4: M0_IN.4, M0_OUT.4
  N5: H0.1, H01.1
  N6: H0.2, H01.2
  N7: H01.3, H1.1
  N8: H01.4, H1.2
  N9: T01.1, TE.T0
  GND: T01.2, T01.4, T23.2, T23.4, ES2.2, ES1.2, ES0.2, ESZ.3, TE.GND
  N10: T01.3, TE.T1
  N11: T23.1, TE.T2
  N12: T23.3, TE.T3
  N13: ES2.1, TE.ES2
  N14: ES1.1, TE.ES1
  N15: ES0.1, TE.ES0
  N16: M1_OUT.1, M1_IN.1
  N17: M1_OUT.2, M1_IN.2
  N18: M1_OUT.3, M1_IN.3
  N19: M1_OUT.4, M1_IN.4
  N20: M2_OUT.1, M2_IN.1
  N21: M2_OUT.2, M2_IN.2
  N22: M2_OUT.3, M2_IN.3
  N23: M2_OUT.4, M2_IN.4
  N24: M3_OUT.1, M3_IN.1
  N25: M3_OUT.2, M3_IN.2
  N26: M3_OUT.3, M3_IN.3
  N27: M3_OUT.4, M3_IN.4
  N28: H23.1, H2.1
  N29: H23.2, H2.2
  N30: H23.3, H3.1
  N31: H23.4, H3.2
  N32: ESZ.1, TE.ESZ
  5V: ESZ.2, TE.5V

custom parts:
  Header 5x2: Header 5x2 Standard 10-pin dual row 0.1 header. Commonly used with AVR-ISP. Use with Spark Fun Electronics SKU: PRT-00778
